// Digital circuit display.dig as structural Verilog
module display (
  input  clock,
  input  enable,
  input  [15:0] Character_Data,
  output [3:0] R,
  output [3:0] G,
  output [3:0] B,
  output H_output,
  output V_output,
  output [10:0] Character_Address
);

  wire character_position_1_p3, character_position_1_p4, character_position_1_p5, character_position_1_p6,
       strings_4_p15, strings_4_p16, strings_4_p17, sync_1_horizontal, sync_1_picture, sync_1_vertical;
  wire [6:0] strings_1_p19, strings_2_character_o, strings_3_character_o;
  wire [7:0] strings_1_p15, strings_1_p16, strings_2_cx_o, strings_2_cy_o, strings_3_cx_o, strings_3_cy_o;
  wire [11:0] strings_1_p17, strings_1_p18, strings_2_background_o, strings_2_foreground_o,
       strings_3_background_o, strings_3_foreground_o;
  wire [15:0] sync_1_x, sync_1_y;

  sync sync_1 (
    .clock(clock), .Horizontal(sync_1_horizontal), .Vertical(sync_1_vertical), .picture(sync_1_picture),
    .X(sync_1_x), .Y(sync_1_y));
  // character_position character_position_1: pin names not known; wires that end beside it: sync_1_x, sync_1_y, character_position_1_p3, character_position_1_p4, character_position_1_p5, character_position_1_p6
  // strings strings_1: pin names not known; wires that end beside it: character_position_1_p5, character_position_1_p6, 12'h9e, 12'h1, {7{1'b0}}, 12'h3c1, 12'h1, 6'b001000, {8{1'b0}}, 7'b0111000, 7'b0101101, 7'b1000010, 7'b1010101, enable, strings_1_p15, strings_1_p16, strings_1_p17, strings_1_p18, strings_1_p19
  strings strings_2 (
    .CX(strings_1_p15), .CY(strings_1_p16), .foreground(strings_1_p17), .background(strings_1_p18),
    .character(strings_1_p19), .foreground__colour(12'h3c1), .background__colour(12'h1),
    .CX__colour(6'b001001), .CY_colour({8{1'b0}}), .Character_0(7'b1010100), .Character_1(7'b0100000),
    .Character_2(7'b1001101), .Character_3(7'b1001001), .enable(enable), .CX_o(strings_2_cx_o),
    .CY_o(strings_2_cy_o), .foreground_o(strings_2_foreground_o), .background_o(strings_2_background_o),
    .character_o(strings_2_character_o));
  strings strings_3 (
    .CX(strings_2_cx_o), .CY(strings_2_cy_o), .foreground(strings_2_foreground_o),
    .background(strings_2_background_o), .character(strings_2_character_o), .foreground__colour(12'h3c1),
    .background__colour(12'h1), .CX__colour(6'b001010), .CY_colour({8{1'b0}}), .Character_0(7'b1000111),
    .Character_1(7'b1001000), .Character_2(7'b1010100), .Character_3(7'b1011001), .enable(enable),
    .CX_o(strings_3_cx_o), .CY_o(strings_3_cy_o), .foreground_o(strings_3_foreground_o),
    .background_o(strings_3_background_o), .character_o(strings_3_character_o));
  // strings strings_4: pin names not known; wires that end beside it: strings_3_cx_o, strings_3_cy_o, strings_3_foreground_o, strings_3_background_o, strings_3_character_o, 12'h3c1, 12'h1, 6'b001011, {8{1'b0}}, 7'b0100000, 7'b1010110, 7'b1000111, 7'b1000001, enable, strings_4_p15, strings_4_p16, strings_4_p17
  // text text_1: pin names not known; wires that end beside it: sync_1_horizontal, sync_1_vertical, sync_1_picture, character_position_1_p3, character_position_1_p4, clock, strings_4_p15, strings_4_p16, strings_4_p17, Character_Data, R, G, B, H_output, V_output, Character_Address

  // Other names for the same wires on the sheet: C = clock

  // Notes on the sheet:
  //   clock: Hz: 2147483647
endmodule
