// Digital circuit strings.dig as structural Verilog
module strings (
  input  [7:0] CX,
  input  [7:0] CY,
  input  [11:0] foreground,
  input  [11:0] background,
  input  [6:0] character,
  input  [11:0] foreground__colour,
  input  [11:0] background__colour,
  input  [5:0] CX__colour,
  input  [7:0] CY_colour,
  input  [6:0] Character_0,
  input  [6:0] Character_1,
  input  [6:0] Character_2,
  input  [6:0] Character_3,
  input  [7:0] cutoff,
  input  enable,
  output [7:0] CX_o,
  output [7:0] CY_o,
  output [11:0] foreground_o,
  output [11:0] background_o,
  output [6:0] character_o
);

  wire and_1_out, comparator_1_eq, comparator_2_eq, comparator_3_eq;
  wire [6:0] multiplexer_1_out;

  Multiplexer #(.Selector_Bits(2), .Bits(7)) multiplexer_1 (
    .sel(CX[1:0]), .in_0(Character_0), .in_1(Character_1), .in_2(Character_2), .in_3(Character_3),
    .out(multiplexer_1_out));
  Comparator #(.Bits(8)) comparator_1 (.a(cutoff), .b(CY), .eq(comparator_1_eq));  // open: gt, lt
  Comparator #(.Bits(6)) comparator_2 (.a(CX[7:2]), .b(CX__colour), .eq(comparator_2_eq));  // open: gt, lt
  Comparator #(.Bits(8)) comparator_3 (.a(CY), .b(CY_colour), .eq(comparator_3_eq));  // open: gt, lt
  and and_1 (and_1_out, comparator_2_eq, enable, comparator_1_eq, comparator_3_eq);
  Multiplexer #(.Bits(7)) multiplexer_2 (
    .sel(and_1_out), .in_0(character), .in_1(multiplexer_1_out), .out(character_o));
  Multiplexer #(.Bits(12)) multiplexer_3 (
    .sel(and_1_out), .in_0(foreground), .in_1(foreground__colour), .out(foreground_o));
  Multiplexer #(.Bits(12)) multiplexer_4 (
    .sel(and_1_out), .in_0(background), .in_1(background__colour), .out(background_o));

  assign CX_o = CX;
  assign CY_o = CY;
endmodule
