// Digital circuit vga.dig as structural Verilog
module vga (
  input  clock
);

  wire vga_display_1_p3, vga_display_1_p4, vga_display_1_p5, vga_display_1_p6, vga_display_1_p7;
  wire [10:0] vga_display_1_p8;
  wire [15:0] Character_ROM_d, vga_display_1_p2;

  // vga_display vga_display_1: pin names not known; wires that end beside it: clock, vga_display_1_p2, vga_display_1_p3, vga_display_1_p4, vga_display_1_p5, vga_display_1_p6, vga_display_1_p7, vga_display_1_p8
  D_FF #(.Bits(16)) d_ff_1 (.D(Character_ROM_d), .C(clock), .Q(vga_display_1_p2));  // open: nQ
  ROM #(.AddrBits(11), .Bits(16)) Character_ROM (.A(vga_display_1_p8), .sel(1'b1), .D(Character_ROM_d));
  VGA vga_1 (
    .R(vga_display_1_p3), .G(vga_display_1_p4), .B(vga_display_1_p5), .H(vga_display_1_p6),
    .V(vga_display_1_p7), .C(clock));

  // Other names for the same wires on the sheet: C = clock

  // Notes on the sheet:
  //   clock: Hz: 2147483647
  //   contents of Character_ROM (hex, n*v repeats v):
  //   35*0,8*180,0,0,8*180,12*0,3e7c,1e78,30*0,3e7c,3ffc,4182,6*6186
  //   ,4182,3e7c,3e7c,4182,6*6186,4182,3ffc,3e7c,10*0,3e7c,3ff8,4180
  //   ,6*6180,4180,3e7c,3e7c,182,6*186,182,1ffc,3e7c,10*0,3e00,3f00
  //   ,4188,6188,6198,61b0,61b0,61e0,61e0,4180,3e7c,3e7c,182,786,786
  //   ,d86,d86,1986,1186,1182,fc,7c,10*0,3e00,3f00,4180,6*6180,4180
  //   ,3f00,3e00,4000,6060,6060,6030,6030,6018,6008,4000,3e78,3e7c,12*0
  //   ,8,8,18,30,30,60,60,23*0,7c,78,200,600,600,c00,800,1800,1000,4*0
  //   ,1000,1800,800,c00,600,600,200,78,7c,10*0,3e00,1e00,40,60,60,30
  //   ,10,18,8,4*0,8,18,10,30,60,60,40,1e00,3e00,12*0,1188,1188,1998
  //   ,db0,db0,7e0,7e0,180,3e7c,3e7c,180,7e0,7e0,db0,db0,1998,1188,1188
  //   ,14*0,8*180,3e7c,3e7c,8*180,25*0,600,600,c00,c00,1800,1000,1000
  //   ,22*0,3e7c,3e7c,40*0,180,180,12*0,8,8,18,30,30,60,60,4*0,600,600
  //   ,c00,c00,1800,1000,1000,12*0,3e7c,3e7c,4006,600e,601a,6032,6036
  //   ,6066,6066,6006,0,0,6006,6606,6606,6c06,4c06,5806,7006,6002,3e7c,3e7c
  //   ,10*0,3e00,1f00,8*180,0,0,8*180,1ff8,3e7c,10*0,3e7c,1e7c,2,6*6
  //   ,2,3e7c,3e7c,4000,6*6000,4000,3e78,3e7c,10*0,3e7c,1e7c,2,6*6,2
  //   ,3e7c,3e7c,2,6*6,2,1e7c,3e7c,11*0,4002,7*6006,4002,3e7c,3e7c,2
  //   ,7*6,2,11*0,3e7c,3e78,4000,6*6000,4000,3e7c,3e7c,2,6*6,2,1e7c
  //   ,3e7c,10*0,3e7c,3e78,4000,6*6000,4000,3e7c,3e7c,4002,6*6006,4002
  //   ,3e7c,3e7c,10*0,3e7c,1e7c,2,7*6,0,0,8*6,2,11*0,3e7c,3e7c,4002
  //   ,6*6006,4002,3e7c,3e7c,4002,6*6006,4002,3e7c,3e7c,10*0,3e7c,3e7c
  //   ,4002,6*6006,4002,3e7c,3e7c,2,6*6,2,1e7c,3e7c,15*0,180,180,8*0
  //   ,180,180,17*0,8*180,0,0,0,600,600,c00,c00,1800,1000,1000,14*0
  //   ,40,c0,c0,180,180,300,300,4*0,300,300,180,180,c0,c0,40,17*0,3e7c,3e7c
  //   ,8*0,1e78,3e7c,17*0,200,300,300,180,180,c0,c0,4*0,c0,c0,180,180
  //   ,300,300,200,12*0,3e7c,1e7c,2,6*6,2,7c,fc,8*180,12*0,3e7c,3ffc
  //   ,4182,6*6186,6182,fc,7c,7*6000,4000,3e78,3e7c,10*0,3e7c,3e7c,4002
  //   ,6*6006,4002,3e7c,3e7c,4002,7*6006,4002,11*0,3e7c,1ffc,182,6*186
  //   ,182,3e7c,3e7c,182,6*186,182,1ffc,3e7c,10*0,3e7c,3e78,4000,7*6000
  //   ,0,0,7*6000,4000,3e78,3e7c,10*0,3e7c,1ffc,182,7*186,0,0,7*186
  //   ,182,1ffc,3e7c,10*0,3e7c,3e78,4000,6*6000,4000,3e7c,3e7c,4000
  //   ,6*6000,4000,3e78,3e7c,10*0,3e7c,3e78,4000,6*6000,4000,3e7c,3e7c
  //   ,4000,7*6000,4000,11*0,3e7c,3e78,4000,7*6000,7c,7c,6002,6*6006
  //   ,4002,3e7c,3e7c,11*0,4002,7*6006,4002,3e7c,3e7c,4002,7*6006,4002
  //   ,11*0,3e7c,1ff8,8*180,0,0,8*180,1ff8,3e7c,10*0,7c,7c,2,7*6,0,0
  //   ,7*6006,4002,3e7c,3e7c,11*0,4000,6008,6008,6018,6030,6030,6060,6060
  //   ,4000,3e00,3e00,4000,6060,6060,6030,6030,6018,6008,6008,4000,12*0
  //   ,4000,8*6000,0,0,7*6000,4000,3e78,3e7c,11*0,4002,6006,700e,581a
  //   ,4c32,6c36,6666,6666,6006,0,0,8*6186,4002,12*0,4002,6006,7006
  //   ,5806,4c06,6c06,6606,6606,6006,0,0,6006,6066,6066,6036,6032,601a
  //   ,600e,6006,4002,11*0,3e7c,3e7c,4002,7*6006,0,0,7*6006,4002,3e7c,3e7c
  //   ,10*0,3e7c,3e7c,4002,6*6006,4002,3e7c,3e7c,4000,7*6000,4000,11*0
  //   ,3e7c,3e7c,4002,7*6006,0,0,6006,6066,6066,6036,6032,601a,600e
  //   ,4006,3e7c,3e7c,10*0,3e7c,3e7c,4002,6*6006,4006,3e00,3e00,4000
  //   ,6060,6060,6030,6030,6018,6008,6008,4000,11*0,3e7c,3e78,4000,6*6000
  //   ,4000,3e7c,3e7c,2,6*6,2,1e7c,3e7c,10*0,3e7c,1ff8,8*180,0,0,8*180
  //   ,13*0,4002,8*6006,0,0,7*6006,4002,3e7c,3e7c,11*0,4000,6008,6008
  //   ,6018,6030,6030,6060,6060,6000,0,0,6000,6600,6600,6c00,4c00,5800
  //   ,7000,6000,4000,12*0,4002,8*6006,0,0,7*6186,4182,3ffc,3e7c,12*0
  //   ,1008,1008,1818,c30,c30,660,660,4*0,660,660,c30,c30,1818,1008,1008
  //   ,14*0,1008,1008,1818,c30,c30,660,660,0,0,0,8*180,12*0,3e7c,1e78
  //   ,0,8,18,30,30,60,60,4*0,600,600,c00,c00,1800,1000,0,1e78,3e7c
  //   ,10*0,3e00,3e00,4000,7*6000,0,0,7*6000,4000,3e00,3e00,12*0,1000,1000
  //   ,1800,c00,c00,600,600,4*0,60,60,30,30,18,8,8,12*0,7c,7c,2,7*6
  //   ,0,0,7*6,2,7c,7c,12*0,240,660,660,c30,810,1818,1008,43*0,1e78,3e7c
endmodule
